// Logisim project Cannon_Game.circ as structural Verilog: 1 circuit, main circuit main
module main (
);

  wire clock_1_out, controlled_buffer_1_out, keyboard_1_avail, main_1_activate, main_2_ground;
  wire [3:0] main_1_y;
  wire [4:0] main_1_x;
  wire [6:0] keyboard_1_data;
  wire [7:0] \main_1_liczba_dziesiątek , \main_1_liczba_jedności , main_2_hsd, main_2_hsj, main_2_lives,
       main_2_wd, main_2_wj;
  wire [15:0] main_2__0, main_2__1, main_2__2, main_2__3, main_2__4, main_2__5, main_2__6, main_2__7,
       main_2__8, main_2__9, main_2__10, main_2__11, main_2__12, main_2__13, main_2__14, main_2__15,
       main_2__16, main_2__17, main_2__18, main_2__19, main_2__20, main_2__21, main_2__22, main_2__23,
       main_2__24, main_2__25, main_2__26, main_2__27, main_2__28, main_2__29, main_2__30, main_2__31;

  assign controlled_buffer_1_out = keyboard_1_avail ? clock_1_out : 1'bz;  // Controlled_Buffer controlled_buffer_1
  Clock clock_1 (.out(clock_1_out));
  Pull_Resistor pull_resistor_1 (.node(controlled_buffer_1_out));
  Keyboard #(.buflen(1)) keyboard_1 (
    .clk(controlled_buffer_1_out), .re(1'b1), .avail(keyboard_1_avail), .data(keyboard_1_data));  // open: clr
  ustawianie_kata_wyswietlanie_kata_main main_1 (
    .\Liczba_jedności (\main_1_liczba_jedności ), .\Liczba_dziesiątek (\main_1_liczba_dziesiątek ),
    .X(main_1_x), .Y(main_1_y), .Ground_Hit(main_2_ground), .Keyboard_input(keyboard_1_data),
    .Activate(main_1_activate));
  _7_Segment_Display u_7_segment_display_1 (
    .g(\main_1_liczba_dziesiątek [0]), .f(\main_1_liczba_dziesiątek [1]), .a(\main_1_liczba_dziesiątek [2]),
    .b(\main_1_liczba_dziesiątek [3]), .e(\main_1_liczba_dziesiątek [4]), .d(\main_1_liczba_dziesiątek [5]),
    .c(\main_1_liczba_dziesiątek [6]), .dp(\main_1_liczba_dziesiątek [7]));
  _7_Segment_Display u_7_segment_display_2 (
    .g(\main_1_liczba_jedności [0]), .f(\main_1_liczba_jedności [1]), .a(\main_1_liczba_jedności [2]),
    .b(\main_1_liczba_jedności [3]), .e(\main_1_liczba_jedności [4]), .d(\main_1_liczba_jedności [5]),
    .c(\main_1_liczba_jedności [6]), .dp(\main_1_liczba_jedności [7]));
  DotMatrix #(.matrixcols(32), .matrixrows(16)) dotmatrix_1 (
    .col0(main_2__0), .col1(main_2__1), .col2(main_2__2), .col3(main_2__3), .col4(main_2__4),
    .col5(main_2__5), .col6(main_2__6), .col7(main_2__7), .col8(main_2__8), .col9(main_2__9),
    .col10(main_2__10), .col11(main_2__11), .col12(main_2__12), .col13(main_2__13), .col14(main_2__14),
    .col15(main_2__15), .col16(main_2__16), .col17(main_2__17), .col18(main_2__18), .col19(main_2__19),
    .col20(main_2__20), .col21(main_2__21), .col22(main_2__22), .col23(main_2__23), .col24(main_2__24),
    .col25(main_2__25), .col26(main_2__26), .col27(main_2__27), .col28(main_2__28), .col29(main_2__29),
    .col30(main_2__30), .col31(main_2__31));
  _7_Segment_Display u_7_segment_display_3 (
    .g(main_2_wd[0]), .f(main_2_wd[1]), .a(main_2_wd[2]), .b(main_2_wd[3]), .e(main_2_wd[4]),
    .d(main_2_wd[5]), .c(main_2_wd[6]), .dp(main_2_wd[7]));
  _7_Segment_Display u_7_segment_display_4 (
    .g(main_2_wj[0]), .f(main_2_wj[1]), .a(main_2_wj[2]), .b(main_2_wj[3]), .e(main_2_wj[4]),
    .d(main_2_wj[5]), .c(main_2_wj[6]), .dp(main_2_wj[7]));
  _7_Segment_Display u_7_segment_display_5 (
    .g(main_2_lives[0]), .f(main_2_lives[1]), .a(main_2_lives[2]), .b(main_2_lives[3]), .e(main_2_lives[4]),
    .d(main_2_lives[5]), .c(main_2_lives[6]), .dp(main_2_lives[7]));
  _7_Segment_Display u_7_segment_display_6 (
    .g(main_2_hsd[0]), .f(main_2_hsd[1]), .a(main_2_hsd[2]), .b(main_2_hsd[3]), .e(main_2_hsd[4]),
    .d(main_2_hsd[5]), .c(main_2_hsd[6]), .dp(main_2_hsd[7]));
  _7_Segment_Display u_7_segment_display_7 (
    .g(main_2_hsj[0]), .f(main_2_hsj[1]), .a(main_2_hsj[2]), .b(main_2_hsj[3]), .e(main_2_hsj[4]),
    .d(main_2_hsj[5]), .c(main_2_hsj[6]), .dp(main_2_hsj[7]));
  Obsluga_wyswietlacza_main main_2 (
    .Bullet_X(main_1_x), .Bullet_Y(main_1_y), .Activate(main_1_activate), .Ground(main_2_ground),
    ._0(main_2__0), ._1(main_2__1), ._2(main_2__2), ._3(main_2__3), ._4(main_2__4), ._5(main_2__5),
    ._6(main_2__6), ._7(main_2__7), ._8(main_2__8), ._9(main_2__9), ._10(main_2__10), ._11(main_2__11),
    ._12(main_2__12), ._13(main_2__13), ._14(main_2__14), ._15(main_2__15), ._16(main_2__16),
    ._17(main_2__17), ._18(main_2__18), ._19(main_2__19), ._20(main_2__20), ._21(main_2__21),
    ._22(main_2__22), ._23(main_2__23), ._24(main_2__24), ._25(main_2__25), ._26(main_2__26),
    ._27(main_2__27), ._28(main_2__28), ._29(main_2__29), ._30(main_2__30), ._31(main_2__31), .WJ(main_2_wj),
    .WD(main_2_wd), .HSJ(main_2_hsj), .HSD(main_2_hsd), .Lives(main_2_lives));

  // Notes on the sheet:
  //   CONTROLS
  //   Angle values
  //   Press W to increase
  //   Press S to decrease
  //   Projectile
  //   Press SPACE to fire
  //   Game
  //   Press D to restart
  //   ANGLE
  //   SCORE
  //   LIVES
  //   RECORD
endmodule
