// Logisim project Obsluga_wyswietlacza.circ as structural Verilog: 1 circuit, main circuit main
module main (
  input  [4:0] Bullet_X,
  input  [3:0] Bullet_Y,
  input  Activate,
  output [15:0] _0,
  output [15:0] _2,
  output [15:0] _4,
  output [15:0] _6,
  output [15:0] _8,
  output [15:0] _10,
  output [15:0] _12,
  output [15:0] _14,
  output [15:0] _16,
  output [15:0] _18,
  output [15:0] _20,
  output [15:0] _22,
  output [15:0] _24,
  output [15:0] _26,
  output [15:0] _28,
  output [15:0] _30,
  output [15:0] _1,
  output [15:0] _3,
  output [15:0] _5,
  output [15:0] _7,
  output [15:0] _9,
  output [15:0] _11,
  output [15:0] _13,
  output [15:0] _15,
  output [15:0] _17,
  output [15:0] _19,
  output [15:0] _21,
  output [15:0] _23,
  output [15:0] _25,
  output [15:0] _27,
  output [15:0] _29,
  output [15:0] _31,
  output [7:0] HSJ,
  output [7:0] HSD,
  output Ground,
  output [7:0] WJ,
  output [7:0] WD,
  output [7:0] Lives
);

  wire clock_1_out, comparator_1_gt, main_2_is_alive, main_2_plus_score, not_1_out, not_2_out;
  wire [2:0] main_2_lives;
  wire [6:0] controlled_buffer_1_out, counter_1_q, register_1_q;
  wire [15:0] and_1_out, and_2_out, and_3_out, and_4_out, main_1__0, main_1__1, main_1__2, main_1__3,
       main_1__4, main_1__5, main_1__6, main_1__7, main_1__8, main_1__9, main_1__10, main_1__11, main_1__12,
       main_1__13, main_1__14, main_1__15, main_1__16, main_1__17, main_1__18, main_1__19, main_1__20,
       main_1__21, main_1__22, main_1__23, main_1__24, main_1__25, main_1__26, main_1__27, main_1__28,
       main_1__29, main_1__30, main_1__31, main_2_out_4, main_2_out_5, main_2_out_6, main_2_out_7,
       main_2_out_8, main_2_out_9, main_2_out_10, main_2_out_11, main_2_out_12, main_2_out_13, main_2_out_14,
       main_2_out_15, main_2_out_16, main_2_out_17, main_2_out_18, main_2_out_19, main_2_out_21,
       main_2_out_22, main_2_out_23, main_2_out_24, main_2_out_25, main_2_out_26, main_2_out_27,
       main_2_out_28, main_2_out_29, main_2_out_30, main_2_out_31, main_2_out_32, main_2_out_33,
       main_2_out_34, main_2_out_35, main_2_out_36;

  assign and_1_out = 16'h30 & 16'h30;  // AND_Gate and_1, 16 bits wide
  assign and_2_out = 16'h6 & 16'h6;  // AND_Gate and_2, 16 bits wide
  assign and_3_out = 16'hc & 16'hc;  // AND_Gate and_3, 16 bits wide
  assign and_4_out = 16'h18 & 16'h18;  // AND_Gate and_4, 16 bits wide
  assign _0 = main_1__0 | and_2_out | main_2_out_4;  // OR_Gate or_1, 16 bits wide
  Wyswietlacz_pocisku_main main_1 (
    .X_bullet(Bullet_X), .Y_bullet(Bullet_Y), ._0(main_1__0), ._1(main_1__1), ._2(main_1__2), ._3(main_1__3),
    ._4(main_1__4), ._5(main_1__5), ._6(main_1__6), ._7(main_1__7), ._8(main_1__8), ._9(main_1__9),
    ._10(main_1__10), ._11(main_1__11), ._12(main_1__12), ._13(main_1__13), ._14(main_1__14),
    ._15(main_1__15), ._16(main_1__16), ._17(main_1__17), ._18(main_1__18), ._19(main_1__19),
    ._20(main_1__20), ._21(main_1__21), ._22(main_1__22), ._23(main_1__23), ._24(main_1__24),
    ._25(main_1__25), ._26(main_1__26), ._27(main_1__27), ._28(main_1__28), ._29(main_1__29),
    ._30(main_1__30), ._31(main_1__31));
  assign _1 = main_1__1 | and_3_out | main_2_out_21;  // OR_Gate or_2, 16 bits wide
  assign _2 = main_1__2 | and_4_out | main_2_out_5;  // OR_Gate or_3, 16 bits wide
  assign _4 = main_1__4 | main_2_out_6;  // OR_Gate or_4, 16 bits wide
  assign _3 = main_1__3 | and_1_out | main_2_out_22;  // OR_Gate or_5, 16 bits wide
  assign _5 = main_1__5 | main_2_out_23;  // OR_Gate or_6, 16 bits wide
  assign _6 = main_1__6 | main_2_out_7;  // OR_Gate or_7, 16 bits wide
  assign _8 = main_1__8 | main_2_out_8;  // OR_Gate or_8, 16 bits wide
  assign _7 = main_1__7 | main_2_out_24;  // OR_Gate or_9, 16 bits wide
  assign _9 = main_1__9 | main_2_out_25;  // OR_Gate or_10, 16 bits wide
  assign _10 = main_1__10 | main_2_out_9;  // OR_Gate or_11, 16 bits wide
  assign _12 = main_1__12 | main_2_out_10;  // OR_Gate or_12, 16 bits wide
  assign _11 = main_1__11 | main_2_out_26;  // OR_Gate or_13, 16 bits wide
  assign _13 = main_1__13 | main_2_out_27;  // OR_Gate or_14, 16 bits wide
  Wyswietlacz_przeciwnikow_main main_2 (
    .Bullet_X(Bullet_X), .Bullet_Y(Bullet_Y), .Ground(Ground), .plus_score(main_2_plus_score),
    .out_4(main_2_out_4), .Lives(main_2_lives), .Activate(Activate), .Is_Alive(main_2_is_alive),
    .out_21(main_2_out_21), .out_5(main_2_out_5), .out_22(main_2_out_22), .out_6(main_2_out_6),
    .out_23(main_2_out_23), .out_7(main_2_out_7), .out_24(main_2_out_24), .out_8(main_2_out_8),
    .out_9(main_2_out_9), .out_10(main_2_out_10), .out_11(main_2_out_11), .out_25(main_2_out_25),
    .out_26(main_2_out_26), .out_27(main_2_out_27), .out_28(main_2_out_28), .out_12(main_2_out_12),
    .out_13(main_2_out_13), .out_14(main_2_out_14), .out_15(main_2_out_15), .out_16(main_2_out_16),
    .out_17(main_2_out_17), .out_18(main_2_out_18), .out_19(main_2_out_19), .out_29(main_2_out_29),
    .out_30(main_2_out_30), .out_31(main_2_out_31), .out_32(main_2_out_32), .out_33(main_2_out_33),
    .out_34(main_2_out_34), .out_35(main_2_out_35), .out_36(main_2_out_36));
  assign _14 = main_1__14 | main_2_out_11;  // OR_Gate or_15, 16 bits wide
  not not_1 (not_1_out, main_2_is_alive);
  assign _16 = main_1__16 | main_2_out_12;  // OR_Gate or_16, 16 bits wide
  assign _15 = main_1__15 | main_2_out_28;  // OR_Gate or_17, 16 bits wide
  assign _17 = main_1__17 | main_2_out_29;  // OR_Gate or_18, 16 bits wide
  Clock clock_1 (.out(clock_1_out));
  assign _18 = main_1__18 | main_2_out_13;  // OR_Gate or_19, 16 bits wide
  Counter #(.width(7), .max('h63), .ongoal("stay")) counter_1 (
    .Q(counter_1_q), .clk(main_2_plus_score), .clr(not_1_out));  // open: load, D, count, carry
  assign _20 = main_1__20 | main_2_out_14;  // OR_Gate or_20, 16 bits wide
  assign _19 = main_1__19 | main_2_out_30;  // OR_Gate or_21, 16 bits wide
  not not_2 (not_2_out, comparator_1_gt);
  Comparator #(.width(7)) comparator_1 (.a(register_1_q), .b(counter_1_q), .gt(comparator_1_gt));  // open: eq, lt
  assign _21 = main_1__21 | main_2_out_31;  // OR_Gate or_22, 16 bits wide
  assign controlled_buffer_1_out = not_2_out ? counter_1_q : 7'bz;  // Controlled_Buffer controlled_buffer_1
  assign _22 = main_1__22 | main_2_out_15;  // OR_Gate or_23, 16 bits wide
  Register #(.width(7), .trigger("falling")) register_1 (
    .D(controlled_buffer_1_out), .Q(register_1_q), .clk(clock_1_out));  // open: en, clr
  ROM #(.addrWidth(7), .dataWidth(16)) rom_1 (.addr(counter_1_q), .data({WD, WJ}));  // open: sel
  ROM #(.addrWidth(3)) rom_2 (.addr(main_2_lives), .data(Lives));  // open: sel
  assign _24 = main_1__24 | main_2_out_16;  // OR_Gate or_24, 16 bits wide
  assign _23 = main_1__23 | main_2_out_32;  // OR_Gate or_25, 16 bits wide
  assign _25 = main_1__25 | main_2_out_33;  // OR_Gate or_26, 16 bits wide
  assign _26 = main_1__26 | main_2_out_17;  // OR_Gate or_27, 16 bits wide
  ROM #(.addrWidth(7), .dataWidth(16)) rom_3 (.addr(register_1_q), .data({HSD, HSJ}));  // open: sel
  assign _28 = main_1__28 | main_2_out_18;  // OR_Gate or_28, 16 bits wide
  assign _27 = main_1__27 | main_2_out_34;  // OR_Gate or_29, 16 bits wide
  assign _29 = main_1__29 | main_2_out_35;  // OR_Gate or_30, 16 bits wide
  assign _30 = main_1__30 | main_2_out_19;  // OR_Gate or_31, 16 bits wide
  assign _31 = main_1__31 | main_2_out_36;  // OR_Gate or_32, 16 bits wide

  // Notes on the sheet:
  //   contents of rom_1 (hex, n*v repeats v):
  //   7e7e 7e48 7e3d 7e6d 7e4b 7e67 7ef7 7e4c 7e7f 7eef 487e 4848 483d 486d 484b 4867 48f7 484c 487f 48ef
  //   3d7e 3d48 3d3d 3d6d 3d4b 3d67 3df7 3d4c 3d7f 3def 6d7e 6d48 6d3d 6d6d 6d4b 6d67 6df7 6d4c 6d7f 6def
  //   4b7e 4b48 4b3d 4b6d 4b4b 4b67 4bf7 4b4c 4b7f 4bef 677e 6748 673d 676d 674b 6767 67f7 674c 677f 67ef
  //   f77e f748 f73d f76d f74b f767 f7f7 f74c f77f f7ef 4c7e 4c48 4c3d 4c6d 4c4b 4c67 4cf7 4c4c 4c7f 4cef
  //   7f7e 7f48 7f3d 7f6d 7f4b 7f67 7ff7 7f4c 7f7f 7fef ef7e ef48 ef3d ef6d ef4b ef67 eff7 ef4c ef7f efef
  //   contents of rom_2 (hex, n*v repeats v):
  //   7e 48 3d 6d 4b 67 f7 4c
  //   contents of rom_3 (hex, n*v repeats v):
  //   7e7e 7e48 7e3d 7e6d 7e4b 7e67 7ef7 7e4c 7e7f 7eef 487e 4848 483d 486d 484b 4867 48f7 484c 487f 48ef
  //   3d7e 3d48 3d3d 3d6d 3d4b 3d67 3df7 3d4c 3d7f 3def 6d7e 6d48 6d3d 6d6d 6d4b 6d67 6df7 6d4c 6d7f 6def
  //   4b7e 4b48 4b3d 4b6d 4b4b 4b67 4bf7 4b4c 4b7f 4bef 677e 6748 673d 676d 674b 6767 67f7 674c 677f 67ef
  //   f77e f748 f73d f76d f74b f767 f7f7 f74c f77f f7ef 4c7e 4c48 4c3d 4c6d 4c4b 4c67 4cf7 4c4c 4c7f 4cef
  //   7f7e 7f48 7f3d 7f6d 7f4b 7f67 7ff7 7f4c 7f7f 7fef ef7e ef48 ef3d ef6d ef4b ef67 eff7 ef4c ef7f efef
endmodule
