// Logisim project Sprawdzanie kolizji.circ as structural Verilog: 1 circuit, main circuit main
module main (
  input  [31:0] Enemies_X,
  input  [4:0] Bullet_X,
  input  [3:0] Bullet_Y,
  input  [2:0] in_4,
  input  [2:0] in_5,
  input  [2:0] in_6,
  input  [2:0] in_7,
  input  [2:0] in_8,
  input  [2:0] in_9,
  input  [2:0] in_10,
  input  [2:0] in_11,
  input  [2:0] in_12,
  input  [2:0] in_13,
  input  [2:0] in_14,
  input  [2:0] in_15,
  input  [2:0] in_16,
  input  [2:0] in_17,
  input  [2:0] in_18,
  input  [2:0] in_19,
  input  [2:0] in_20,
  input  [2:0] in_21,
  input  [2:0] in_22,
  input  [2:0] in_23,
  input  [2:0] in_24,
  input  [2:0] in_25,
  input  [2:0] in_26,
  input  [2:0] in_27,
  input  [2:0] in_28,
  input  [2:0] in_29,
  input  [2:0] in_30,
  input  [2:0] in_31,
  input  [2:0] in_32,
  input  [2:0] in_33,
  input  [2:0] in_34,
  input  [2:0] in_35,
  output [31:0] \output ,
  output Reset___trafienie_w_ziemie,
  output [31:0] out_38,
  output plus_Score
);

  wire bitselector_1_out, comparator_1_eq, comparator_1_gt, comparator_2_eq, comparator_3_eq,
       comparator_4_eq, comparator_5_gt, or_2_out;
  wire [2:0] multiplexer_1_out;
  wire [3:0] bit_extender_1_out, subtractor_1_out, subtractor_2_out;
  wire [4:0] not_1_out;
  wire [31:0] not_2_out, not_3_out, not_4_out, not_5_out, not_6_out, pull_resistor_1_node, register_1_q,
       shifter_1_out, shifter_2_out, shifter_3_out, shifter_4_out, shifter_5_out, shifter_6_out;

  assign not_1_out = ~Bullet_X;  // NOT_Gate not_1, 5 bits wide
  assign bit_extender_1_out = {{1{1'b0}}, multiplexer_1_out};  // Bit_Extender bit_extender_1
  Multiplexer #(.select(5), .width(3)) multiplexer_1 (
    .in0(in_4), .in1(in_5), .in2(in_6), .in3(in_7), .in4(in_8), .in5(in_9), .in6(in_10), .in7(in_11),
    .in8(in_12), .in9(in_13), .in10(in_14), .in11(in_15), .in12(in_16), .in13(in_17), .in14(in_18),
    .in15(in_19), .in16(in_20), .in17(in_21), .in18(in_22), .in19(in_23), .in20(in_24), .in21(in_25),
    .in22(in_26), .in23(in_27), .in24(in_28), .in25(in_29), .in26(in_30), .in27(in_31), .in28(in_32),
    .in29(in_33), .in30(in_34), .in31(in_35), .out(multiplexer_1_out), .sel(Bullet_X));  // open: en
  BitSelector #(.width(32)) bitselector_1 (.in(Enemies_X), .out(bitselector_1_out), .sel(not_1_out));
  Subtractor #(.width(4)) subtractor_1 (.a(Bullet_Y), .b(4'b0001), .out(subtractor_1_out));  // open: bin, bout
  Subtractor #(.width(4)) subtractor_2 (.a(Bullet_Y), .b(4'b0010), .out(subtractor_2_out));  // open: bin, bout
  Comparator #(.width(4), .mode("unsigned")) comparator_1 (
    .a(bit_extender_1_out), .b(Bullet_Y), .gt(comparator_1_gt), .eq(comparator_1_eq));  // open: lt
  Comparator #(.width(4), .mode("unsigned")) comparator_2 (
    .a(bit_extender_1_out), .b(subtractor_1_out), .eq(comparator_2_eq));  // open: gt, lt
  Comparator #(.width(4), .mode("unsigned")) comparator_3 (
    .a(bit_extender_1_out), .b(subtractor_2_out), .eq(comparator_3_eq));  // open: gt, lt
  or or_1 (Reset___trafienie_w_ziemie, comparator_1_gt, comparator_1_eq);
  or or_2 (or_2_out, comparator_2_eq, comparator_3_eq);
  Pull_Resistor pull_resistor_1 (.node(pull_resistor_1_node));
  assign pull_resistor_1_node = plus_Score ? 32'h1 : 32'bz;  // Controlled_Buffer controlled_buffer_1
  and and_1 (plus_Score, bitselector_1_out, or_2_out);
  Shifter #(.width(32)) shifter_1 (.in(pull_resistor_1_node), .\dist (not_1_out), .out(shifter_1_out));
  Comparator #(.width(5), .mode("unsigned")) comparator_4 (
    .a(Bullet_X), .b(5'b00100), .eq(comparator_4_eq));  // open: gt, lt
  Register #(.width(32)) register_1 (
    .D(shifter_1_out), .Q(register_1_q), .clk(comparator_5_gt), .clr(comparator_4_eq));  // open: en
  Comparator #(.width(32), .mode("unsigned")) comparator_5 (
    .a(shifter_1_out), .b(register_1_q), .gt(comparator_5_gt));  // open: eq, lt
  Shifter #(.width(32), .shift("lr")) shifter_2 (.in(register_1_q), .\dist (5'b00010), .out(shifter_2_out));
  Shifter #(.width(32), .shift("lr")) shifter_3 (.in(register_1_q), .\dist (5'b00001), .out(shifter_3_out));
  Shifter #(.width(32)) shifter_4 (.in(register_1_q), .\dist ({5{1'b0}}), .out(shifter_4_out));
  Shifter #(.width(32)) shifter_5 (.in(register_1_q), .\dist (5'b00001), .out(shifter_5_out));
  Shifter #(.width(32)) shifter_6 (.in(register_1_q), .\dist (5'b00010), .out(shifter_6_out));
  assign not_2_out = ~shifter_2_out;  // NOT_Gate not_2, 32 bits wide
  assign not_3_out = ~shifter_3_out;  // NOT_Gate not_3, 32 bits wide
  assign not_4_out = ~shifter_4_out;  // NOT_Gate not_4, 32 bits wide
  assign not_5_out = ~shifter_5_out;  // NOT_Gate not_5, 32 bits wide
  assign not_6_out = ~shifter_6_out;  // NOT_Gate not_6, 32 bits wide
  assign \output  = not_2_out & not_3_out & not_4_out & not_5_out & not_6_out;  // AND_Gate and_2, 32 bits wide
  Register #(.width(32), .trigger("falling")) register_2 (.D(\output ), .Q(out_38), .clk(plus_Score));  // open: en, clr
endmodule
