// Logisim project Wyswietlacz_pocisku.circ as structural Verilog: 1 circuit, main circuit main
module main (
  input  [4:0] X_bullet,
  input  [3:0] Y_bullet,
  output [15:0] _1,
  output [15:0] _3,
  output [15:0] _5,
  output [15:0] _7,
  output [15:0] _9,
  output [15:0] _11,
  output [15:0] _13,
  output [15:0] _15,
  output [15:0] _17,
  output [15:0] _19,
  output [15:0] _21,
  output [15:0] _23,
  output [15:0] _25,
  output [15:0] _27,
  output [15:0] _29,
  output [15:0] _31,
  output [15:0] _0,
  output [15:0] _2,
  output [15:0] _4,
  output [15:0] _6,
  output [15:0] _8,
  output [15:0] _10,
  output [15:0] _12,
  output [15:0] _14,
  output [15:0] _16,
  output [15:0] _18,
  output [15:0] _20,
  output [15:0] _22,
  output [15:0] _24,
  output [15:0] _26,
  output [15:0] _28,
  output [15:0] _30
);

  wire demultiplexer_1_out0, demultiplexer_1_out1, demultiplexer_1_out2, demultiplexer_1_out3,
       demultiplexer_1_out4, demultiplexer_1_out5, demultiplexer_1_out6, demultiplexer_1_out7,
       demultiplexer_1_out8, demultiplexer_1_out9, demultiplexer_1_out10, demultiplexer_1_out11,
       demultiplexer_1_out12, demultiplexer_1_out13, demultiplexer_1_out14, demultiplexer_1_out15,
       demultiplexer_1_out16, demultiplexer_1_out17, demultiplexer_1_out18, demultiplexer_1_out19,
       demultiplexer_1_out20, demultiplexer_1_out21, demultiplexer_1_out22, demultiplexer_1_out23,
       demultiplexer_1_out24, demultiplexer_1_out25, demultiplexer_1_out26, demultiplexer_1_out27,
       demultiplexer_1_out28, demultiplexer_1_out29, demultiplexer_1_out30, demultiplexer_1_out31;
  wire [15:0] demultiplexer_2_out0;

  Demultiplexer #(.select(5)) demultiplexer_1 (
    .out0(demultiplexer_1_out0), .out1(demultiplexer_1_out1), .out2(demultiplexer_1_out2),
    .out3(demultiplexer_1_out3), .out4(demultiplexer_1_out4), .out5(demultiplexer_1_out5),
    .out6(demultiplexer_1_out6), .out7(demultiplexer_1_out7), .out8(demultiplexer_1_out8),
    .out9(demultiplexer_1_out9), .out10(demultiplexer_1_out10), .out11(demultiplexer_1_out11),
    .out12(demultiplexer_1_out12), .out13(demultiplexer_1_out13), .out14(demultiplexer_1_out14),
    .out15(demultiplexer_1_out15), .out16(demultiplexer_1_out16), .out17(demultiplexer_1_out17),
    .out18(demultiplexer_1_out18), .out19(demultiplexer_1_out19), .out20(demultiplexer_1_out20),
    .out21(demultiplexer_1_out21), .out22(demultiplexer_1_out22), .out23(demultiplexer_1_out23),
    .out24(demultiplexer_1_out24), .out25(demultiplexer_1_out25), .out26(demultiplexer_1_out26),
    .out27(demultiplexer_1_out27), .out28(demultiplexer_1_out28), .out29(demultiplexer_1_out29),
    .out30(demultiplexer_1_out30), .out31(demultiplexer_1_out31), .in(1'b1), .sel(X_bullet));  // open: en
  Demultiplexer #(.select(4)) demultiplexer_2 (
    .out0(demultiplexer_2_out0[0]), .out1(demultiplexer_2_out0[1]), .out2(demultiplexer_2_out0[2]),
    .out3(demultiplexer_2_out0[3]), .out4(demultiplexer_2_out0[4]), .out5(demultiplexer_2_out0[5]),
    .out6(demultiplexer_2_out0[6]), .out7(demultiplexer_2_out0[7]), .out8(demultiplexer_2_out0[8]),
    .out9(demultiplexer_2_out0[9]), .out10(demultiplexer_2_out0[10]), .out11(demultiplexer_2_out0[11]),
    .out12(demultiplexer_2_out0[12]), .out13(demultiplexer_2_out0[13]), .out14(demultiplexer_2_out0[14]),
    .out15(demultiplexer_2_out0[15]), .in(1'b1), .sel(Y_bullet));  // open: en
  Multiplexer #(.width(16)) multiplexer_1 (
    .in0({16{1'b0}}), .in1(demultiplexer_2_out0), .out(_0), .sel(demultiplexer_1_out0));  // open: en
  Multiplexer #(.width(16)) multiplexer_2 (
    .in0({16{1'b0}}), .in1(demultiplexer_2_out0), .out(_1), .sel(demultiplexer_1_out1));  // open: en
  Multiplexer #(.width(16)) multiplexer_3 (
    .in0({16{1'b0}}), .in1(demultiplexer_2_out0), .out(_2), .sel(demultiplexer_1_out2));  // open: en
  Multiplexer #(.width(16)) multiplexer_4 (
    .in0({16{1'b0}}), .in1(demultiplexer_2_out0), .out(_3), .sel(demultiplexer_1_out3));  // open: en
  Multiplexer #(.width(16)) multiplexer_5 (
    .in0({16{1'b0}}), .in1(demultiplexer_2_out0), .out(_4), .sel(demultiplexer_1_out4));  // open: en
  Multiplexer #(.width(16)) multiplexer_6 (
    .in0({16{1'b0}}), .in1(demultiplexer_2_out0), .out(_5), .sel(demultiplexer_1_out5));  // open: en
  Multiplexer #(.width(16)) multiplexer_7 (
    .in0({16{1'b0}}), .in1(demultiplexer_2_out0), .out(_6), .sel(demultiplexer_1_out6));  // open: en
  Multiplexer #(.width(16)) multiplexer_8 (
    .in0({16{1'b0}}), .in1(demultiplexer_2_out0), .out(_7), .sel(demultiplexer_1_out7));  // open: en
  Multiplexer #(.width(16)) multiplexer_9 (
    .in0({16{1'b0}}), .in1(demultiplexer_2_out0), .out(_8), .sel(demultiplexer_1_out8));  // open: en
  Multiplexer #(.width(16)) multiplexer_10 (
    .in0({16{1'b0}}), .in1(demultiplexer_2_out0), .out(_9), .sel(demultiplexer_1_out9));  // open: en
  Multiplexer #(.width(16)) multiplexer_11 (
    .in0({16{1'b0}}), .in1(demultiplexer_2_out0), .out(_10), .sel(demultiplexer_1_out10));  // open: en
  Multiplexer #(.width(16)) multiplexer_12 (
    .in0({16{1'b0}}), .in1(demultiplexer_2_out0), .out(_11), .sel(demultiplexer_1_out11));  // open: en
  Multiplexer #(.width(16)) multiplexer_13 (
    .in0({16{1'b0}}), .in1(demultiplexer_2_out0), .out(_12), .sel(demultiplexer_1_out12));  // open: en
  Multiplexer #(.width(16)) multiplexer_14 (
    .in0({16{1'b0}}), .in1(demultiplexer_2_out0), .out(_13), .sel(demultiplexer_1_out13));  // open: en
  Multiplexer #(.width(16)) multiplexer_15 (
    .in0({16{1'b0}}), .in1(demultiplexer_2_out0), .out(_14), .sel(demultiplexer_1_out14));  // open: en
  Multiplexer #(.width(16)) multiplexer_16 (
    .in0({16{1'b0}}), .in1(demultiplexer_2_out0), .out(_15), .sel(demultiplexer_1_out15));  // open: en
  Multiplexer #(.width(16)) multiplexer_17 (
    .in0({16{1'b0}}), .in1(demultiplexer_2_out0), .out(_16), .sel(demultiplexer_1_out16));  // open: en
  Multiplexer #(.width(16)) multiplexer_18 (
    .in0({16{1'b0}}), .in1(demultiplexer_2_out0), .out(_17), .sel(demultiplexer_1_out17));  // open: en
  Multiplexer #(.width(16)) multiplexer_19 (
    .in0({16{1'b0}}), .in1(demultiplexer_2_out0), .out(_18), .sel(demultiplexer_1_out18));  // open: en
  Multiplexer #(.width(16)) multiplexer_20 (
    .in0({16{1'b0}}), .in1(demultiplexer_2_out0), .out(_19), .sel(demultiplexer_1_out19));  // open: en
  Multiplexer #(.width(16)) multiplexer_21 (
    .in0({16{1'b0}}), .in1(demultiplexer_2_out0), .out(_20), .sel(demultiplexer_1_out20));  // open: en
  Multiplexer #(.width(16)) multiplexer_22 (
    .in0({16{1'b0}}), .in1(demultiplexer_2_out0), .out(_21), .sel(demultiplexer_1_out21));  // open: en
  Multiplexer #(.width(16)) multiplexer_23 (
    .in0({16{1'b0}}), .in1(demultiplexer_2_out0), .out(_22), .sel(demultiplexer_1_out22));  // open: en
  Multiplexer #(.width(16)) multiplexer_24 (
    .in0({16{1'b0}}), .in1(demultiplexer_2_out0), .out(_23), .sel(demultiplexer_1_out23));  // open: en
  Multiplexer #(.width(16)) multiplexer_25 (
    .in0({16{1'b0}}), .in1(demultiplexer_2_out0), .out(_24), .sel(demultiplexer_1_out24));  // open: en
  Multiplexer #(.width(16)) multiplexer_26 (
    .in0({16{1'b0}}), .in1(demultiplexer_2_out0), .out(_25), .sel(demultiplexer_1_out25));  // open: en
  Multiplexer #(.width(16)) multiplexer_27 (
    .in0({16{1'b0}}), .in1(demultiplexer_2_out0), .out(_26), .sel(demultiplexer_1_out26));  // open: en
  Multiplexer #(.width(16)) multiplexer_28 (
    .in0({16{1'b0}}), .in1(demultiplexer_2_out0), .out(_27), .sel(demultiplexer_1_out27));  // open: en
  Multiplexer #(.width(16)) multiplexer_29 (
    .in0({16{1'b0}}), .in1(demultiplexer_2_out0), .out(_28), .sel(demultiplexer_1_out28));  // open: en
  Multiplexer #(.width(16)) multiplexer_30 (
    .in0({16{1'b0}}), .in1(demultiplexer_2_out0), .out(_29), .sel(demultiplexer_1_out29));  // open: en
  Multiplexer #(.width(16)) multiplexer_31 (
    .in0({16{1'b0}}), .in1(demultiplexer_2_out0), .out(_30), .sel(demultiplexer_1_out30));  // open: en
  Multiplexer #(.width(16)) multiplexer_32 (
    .in0({16{1'b0}}), .in1(demultiplexer_2_out0), .out(_31), .sel(demultiplexer_1_out31));  // open: en
endmodule
