// Logisim project Wyswietlacz_przeciwnikow.circ as structural Verilog: 1 circuit, main circuit main
module main (
  input  Activate,
  input  [4:0] Bullet_X,
  input  [3:0] Bullet_Y,
  output [15:0] out_4,
  output [15:0] out_5,
  output [15:0] out_6,
  output [15:0] out_7,
  output [15:0] out_8,
  output [15:0] out_9,
  output [15:0] out_10,
  output [15:0] out_11,
  output [15:0] out_12,
  output [15:0] out_13,
  output [15:0] out_14,
  output [15:0] out_15,
  output [15:0] out_16,
  output [15:0] out_17,
  output [15:0] out_18,
  output [15:0] out_19,
  output Is_Alive,
  output [15:0] out_21,
  output [15:0] out_22,
  output [15:0] out_23,
  output [15:0] out_24,
  output [15:0] out_25,
  output [15:0] out_26,
  output [15:0] out_27,
  output [15:0] out_28,
  output [15:0] out_29,
  output [15:0] out_30,
  output [15:0] out_31,
  output [15:0] out_32,
  output [15:0] out_33,
  output [15:0] out_34,
  output [15:0] out_35,
  output [15:0] out_36,
  output [2:0] Lives,
  output Ground,
  output plus_score
);

  wire and_1_out, not_1_out;
  wire [2:0] _0x, _1x, _2x, _3x, _4x, _5x, _6x, _7x, _8x, _9x, _10x, _11x, _12x, _13x, _14x, _15x, _16x,
       _17x, _18x, _19x, _20x, _21x, _22x, _23x, _24x, _25x, _26x, _27x, _28x, _29x, _30x, _31x;
  wire [31:0] main_2_output, main_3_enemies_output, main_4_output;

  not not_1 (not_1_out, Is_Alive);
  and and_1 (and_1_out, not_1_out, Activate);
  generowanie_poziomu_main main_1 (
    .Regenerate(and_1_out), ._0(_0x), ._1(_1x), ._2(_2x), ._3(_3x), ._4(_4x), ._5(_5x), ._6(_6x), ._7(_7x),
    ._8(_8x), ._9(_9x), ._10(_10x), ._11(_11x), ._12(_12x), ._13(_13x), ._14(_14x), ._15(_15x), ._16(_16x),
    ._17(_17x), ._18(_18x), ._19(_19x), ._20(_20x), ._21(_21x), ._22(_22x), ._23(_23x), ._24(_24x),
    ._25(_25x), ._26(_26x), ._27(_27x), ._28(_28x), ._29(_29x), ._30(_30x), ._31(_31x));
  generator_przesuwanie_w_lewo_main main_2 (
    .\output (main_2_output), .Aktywne(Is_Alive), .\input (main_4_output));  // open: out_6, Reset, out_5
  obsluga_zyc_main main_3 (
    .Enemies_input(main_2_output), .Lives(Lives), .is_alive(Is_Alive),
    .Enemies_output(main_3_enemies_output), .Reset_lives(Activate));
  Sprawdzanie_kolizji_main main_4 (
    .Enemies_X(main_3_enemies_output), .Bullet_X(Bullet_X), .Bullet_Y(Bullet_Y), .plus_Score(plus_score),
    .Reset___trafienie_w_ziemie(Ground), .\output (main_4_output), .in_4(_0x), .in_5(_1x), .in_6(_2x),
    .in_7(_3x), .in_8(_4x), .in_9(_5x), .in_10(_6x), .in_11(_7x), .in_12(_8x), .in_13(_9x), .in_14(_10x),
    .in_15(_11x), .in_16(_12x), .in_17(_13x), .in_18(_14x), .in_19(_15x), .in_20(_16x), .in_21(_17x),
    .in_22(_18x), .in_23(_19x), .in_24(_20x), .in_25(_21x), .in_26(_22x), .in_27(_23x), .in_28(_24x),
    .in_29(_25x), .in_30(_26x), .in_31(_27x), .in_32(_28x), .in_33(_29x), .in_34(_30x), .in_35(_31x));  // open: out_38
  \Wyświetlacz_mapy_main  main_5 (.Level(_0x), .Enemy(main_2_output[31]), .Output(out_4));
  \Wyświetlacz_mapy_main  main_6 (.Level(_1x), .Enemy(main_2_output[30]), .Output(out_21));
  \Wyświetlacz_mapy_main  main_7 (.Level(_2x), .Enemy(main_2_output[29]), .Output(out_5));
  \Wyświetlacz_mapy_main  main_8 (.Level(_3x), .Enemy(main_2_output[28]), .Output(out_22));
  \Wyświetlacz_mapy_main  main_9 (.Level(_4x), .Enemy(main_2_output[27]), .Output(out_6));
  \Wyświetlacz_mapy_main  main_10 (.Level(_5x), .Enemy(main_2_output[26]), .Output(out_23));
  \Wyświetlacz_mapy_main  main_11 (.Level(_6x), .Enemy(main_2_output[25]), .Output(out_7));
  \Wyświetlacz_mapy_main  main_12 (.Level(_7x), .Enemy(main_2_output[24]), .Output(out_24));
  \Wyświetlacz_mapy_main  main_13 (.Level(_8x), .Enemy(main_2_output[23]), .Output(out_8));
  \Wyświetlacz_mapy_main  main_14 (.Level(_9x), .Enemy(main_2_output[22]), .Output(out_25));
  \Wyświetlacz_mapy_main  main_15 (.Level(_10x), .Enemy(main_2_output[21]), .Output(out_9));
  \Wyświetlacz_mapy_main  main_16 (.Level(_11x), .Enemy(main_2_output[20]), .Output(out_26));
  \Wyświetlacz_mapy_main  main_17 (.Level(_12x), .Enemy(main_2_output[19]), .Output(out_10));
  \Wyświetlacz_mapy_main  main_18 (.Level(_13x), .Enemy(main_2_output[18]), .Output(out_27));
  \Wyświetlacz_mapy_main  main_19 (.Level(_14x), .Enemy(main_2_output[17]), .Output(out_11));
  \Wyświetlacz_mapy_main  main_20 (.Level(_15x), .Enemy(main_2_output[16]), .Output(out_28));
  \Wyświetlacz_mapy_main  main_21 (.Level(_16x), .Enemy(main_2_output[15]), .Output(out_12));
  \Wyświetlacz_mapy_main  main_22 (.Level(_17x), .Enemy(main_2_output[14]), .Output(out_29));
  \Wyświetlacz_mapy_main  main_23 (.Level(_18x), .Enemy(main_2_output[13]), .Output(out_13));
  \Wyświetlacz_mapy_main  main_24 (.Level(_19x), .Enemy(main_2_output[12]), .Output(out_30));
  \Wyświetlacz_mapy_main  main_25 (.Level(_20x), .Enemy(main_2_output[11]), .Output(out_14));
  \Wyświetlacz_mapy_main  main_26 (.Level(_21x), .Enemy(main_2_output[10]), .Output(out_31));
  \Wyświetlacz_mapy_main  main_27 (.Level(_22x), .Enemy(main_2_output[9]), .Output(out_15));
  \Wyświetlacz_mapy_main  main_28 (.Level(_23x), .Enemy(main_2_output[8]), .Output(out_32));
  \Wyświetlacz_mapy_main  main_29 (.Level(_24x), .Enemy(main_2_output[7]), .Output(out_16));
  \Wyświetlacz_mapy_main  main_30 (.Level(_25x), .Enemy(main_2_output[6]), .Output(out_33));
  \Wyświetlacz_mapy_main  main_31 (.Level(_26x), .Enemy(main_2_output[5]), .Output(out_17));
  \Wyświetlacz_mapy_main  main_32 (.Level(_27x), .Enemy(main_2_output[4]), .Output(out_34));
  \Wyświetlacz_mapy_main  main_33 (.Level(_28x), .Enemy(main_2_output[3]), .Output(out_18));
  \Wyświetlacz_mapy_main  main_34 (.Level(_29x), .Enemy(main_2_output[2]), .Output(out_35));
  \Wyświetlacz_mapy_main  main_35 (.Level(_30x), .Enemy(main_2_output[1]), .Output(out_19));
  \Wyświetlacz_mapy_main  main_36 (.Level(_31x), .Enemy(main_2_output[0]), .Output(out_36));
endmodule
