// Logisim project Wyświetlacz_mapy.circ as structural Verilog: 1 circuit, main circuit main
module main (
  input  [2:0] Level,
  input  Enemy,
  output [15:0] Output
);

  wire and_1_out, bit_extender_1_out;
  wire [1:0] bit_extender_2_out;
  wire [2:0] bit_extender_3_out, bit_extender_9_out;
  wire [3:0] bit_extender_4_out, bit_extender_10_out;
  wire [3:3] not_1_out;
  wire [4:0] bit_extender_5_out, bit_extender_11_out;
  wire [5:0] bit_extender_6_out, bit_extender_12_out;
  wire [6:0] bit_extender_7_out, bit_extender_13_out;
  wire [7:0] bit_extender_8_out, bit_extender_14_out;
  wire [8:0] bit_extender_15_out;
  wire [9:0] bit_extender_16_out;
  wire [15:0] bit_extender_17_out, bit_extender_18_out, bit_extender_19_out, bit_extender_20_out,
       bit_extender_21_out, bit_extender_22_out, bit_extender_23_out, bit_extender_24_out,
       bit_extender_25_out, bit_extender_26_out, bit_extender_27_out, bit_extender_28_out,
       bit_extender_29_out, bit_extender_30_out, bit_extender_31_out, bit_extender_32_out;

  not not_1 (not_1_out[3], Enemy);
  and and_1 (and_1_out, 1'b0, 1'b0);
  Bit_Extender #(.in_width(1), .out_width(1), .\type ("one")) bit_extender_1 (.in(1'b1), .out(bit_extender_1_out));
  assign bit_extender_2_out = {{1{1'b1}}, 1'b1};  // Bit_Extender bit_extender_2
  assign bit_extender_3_out = {{2{1'b1}}, 1'b1};  // Bit_Extender bit_extender_3
  assign bit_extender_4_out = {{3{1'b1}}, 1'b1};  // Bit_Extender bit_extender_4
  assign bit_extender_5_out = {{4{1'b1}}, 1'b1};  // Bit_Extender bit_extender_5
  assign bit_extender_6_out = {{5{1'b1}}, 1'b1};  // Bit_Extender bit_extender_6
  assign bit_extender_7_out = {{6{1'b1}}, 1'b1};  // Bit_Extender bit_extender_7
  assign bit_extender_8_out = {{7{1'b1}}, 1'b1};  // Bit_Extender bit_extender_8
  assign bit_extender_9_out = {{2{and_1_out}}, bit_extender_1_out};  // Bit_Extender bit_extender_9
  assign bit_extender_10_out = {{2{and_1_out}}, bit_extender_2_out};  // Bit_Extender bit_extender_10
  assign bit_extender_11_out = {{2{and_1_out}}, bit_extender_3_out};  // Bit_Extender bit_extender_11
  assign bit_extender_12_out = {{2{and_1_out}}, bit_extender_4_out};  // Bit_Extender bit_extender_12
  assign bit_extender_13_out = {{2{and_1_out}}, bit_extender_5_out};  // Bit_Extender bit_extender_13
  assign bit_extender_14_out = {{2{and_1_out}}, bit_extender_6_out};  // Bit_Extender bit_extender_14
  assign bit_extender_15_out = {{2{and_1_out}}, bit_extender_7_out};  // Bit_Extender bit_extender_15
  assign bit_extender_16_out = {{2{and_1_out}}, bit_extender_8_out};  // Bit_Extender bit_extender_16
  assign bit_extender_17_out = {{15{1'b0}}, bit_extender_1_out};  // Bit_Extender bit_extender_17
  assign bit_extender_18_out = {{14{1'b0}}, bit_extender_2_out};  // Bit_Extender bit_extender_18
  assign bit_extender_19_out = {{13{1'b0}}, bit_extender_3_out};  // Bit_Extender bit_extender_19
  assign bit_extender_20_out = {{12{1'b0}}, bit_extender_4_out};  // Bit_Extender bit_extender_20
  assign bit_extender_21_out = {{11{1'b0}}, bit_extender_5_out};  // Bit_Extender bit_extender_21
  assign bit_extender_22_out = {{10{1'b0}}, bit_extender_6_out};  // Bit_Extender bit_extender_22
  assign bit_extender_23_out = {{9{1'b0}}, bit_extender_7_out};  // Bit_Extender bit_extender_23
  assign bit_extender_24_out = {{8{1'b0}}, bit_extender_8_out};  // Bit_Extender bit_extender_24
  assign bit_extender_25_out = {{13{1'b0}}, bit_extender_9_out};  // Bit_Extender bit_extender_25
  assign bit_extender_26_out = {{12{1'b0}}, bit_extender_10_out};  // Bit_Extender bit_extender_26
  assign bit_extender_27_out = {{11{1'b0}}, bit_extender_11_out};  // Bit_Extender bit_extender_27
  assign bit_extender_28_out = {{10{1'b0}}, bit_extender_12_out};  // Bit_Extender bit_extender_28
  assign bit_extender_29_out = {{9{1'b0}}, bit_extender_13_out};  // Bit_Extender bit_extender_29
  assign bit_extender_30_out = {{8{1'b0}}, bit_extender_14_out};  // Bit_Extender bit_extender_30
  assign bit_extender_31_out = {{7{1'b0}}, bit_extender_15_out};  // Bit_Extender bit_extender_31
  assign bit_extender_32_out = {{6{1'b0}}, bit_extender_16_out};  // Bit_Extender bit_extender_32
  Multiplexer #(.select(4), .width(16)) multiplexer_1 (
    .in0(bit_extender_25_out), .in1(bit_extender_26_out), .in2(bit_extender_27_out),
    .in3(bit_extender_28_out), .in4(bit_extender_29_out), .in5(bit_extender_30_out),
    .in6(bit_extender_31_out), .in7(bit_extender_32_out), .in8(bit_extender_17_out),
    .in9(bit_extender_18_out), .in10(bit_extender_19_out), .in11(bit_extender_20_out),
    .in12(bit_extender_21_out), .in13(bit_extender_22_out), .in14(bit_extender_23_out),
    .in15(bit_extender_24_out), .out(Output), .sel({not_1_out[3], Level}));  // open: en
endmodule
