// Logisim project generator_przesuwanie_w_lewo.circ as structural Verilog: 1 circuit, main circuit main
module main (
  input  [31:0] \input ,
  input  Aktywne,
  input  Reset,
  output [31:0] \output ,
  output [31:0] out_5,
  output out_6
);

  wire clock_1_out, comparator_1_eq, comparator_1_lt, comparator_2_lt, comparator_3_eq, comparator_3_gt,
       controlled_buffer_2_out, not_1_out;
  wire [2:0] counter_1_q;
  wire [4:0] bit_extender_1_out, counter_2_q;
  wire [31:0] and_1_out, controlled_buffer_1_out, or_1_out, pull_resistor_3_node, shifter_1_out;

  Counter #(.width(3), .max('h7)) counter_1 (
    .Q(counter_1_q), .clk(comparator_3_eq), .clr(comparator_1_lt));  // open: load, D, count, carry
  Clock clock_1 (.out(clock_1_out));
  Comparator #(.width(3), .mode("unsigned")) comparator_1 (
    .a(3'b111), .b(counter_1_q), .eq(comparator_1_eq), .lt(comparator_1_lt));  // open: gt
  assign controlled_buffer_1_out = controlled_buffer_2_out ? 32'h1 : 32'bz;  // Controlled_Buffer controlled_buffer_1
  assign controlled_buffer_2_out = Aktywne ? comparator_1_eq : 1'bz;  // Controlled_Buffer controlled_buffer_2
  Pull_Resistor pull_resistor_1 (.node(controlled_buffer_2_out));
  not not_1 (not_1_out, Aktywne);
  Pull_Resistor pull_resistor_2 (.node(controlled_buffer_1_out));
  Pull_Resistor pull_resistor_3 (.node(pull_resistor_3_node));
  assign pull_resistor_3_node = Aktywne ? shifter_1_out : 32'bz;  // Controlled_Buffer controlled_buffer_3
  assign or_1_out = controlled_buffer_1_out | pull_resistor_3_node;  // OR_Gate or_1, 32 bits wide
  Register #(.width(32)) register_1 (.D(or_1_out), .Q(\output ), .clk(clock_1_out), .clr(not_1_out));  // open: en
  DotMatrix #(.inputtype("row"), .matrixcols(32), .matrixrows(1)) dotmatrix_1 (.row0(\output ));
  assign and_1_out = \output  & \input ;  // AND_Gate and_1, 32 bits wide
  Comparator #(.width(32), .mode("unsigned")) comparator_2 (
    .a(\input ), .b({32{1'b1}}), .lt(comparator_2_lt));  // open: gt, eq
  Shifter #(.width(32)) shifter_1 (.in(and_1_out), .\dist (bit_extender_1_out), .out(shifter_1_out));
  Register #(.width(32)) register_2 (.D(\input ), .Q(out_5), .clk(comparator_2_lt));  // open: en, clr
  D_Flip_Flop d_ff_1 (.clk(comparator_2_lt), .D(1'b1), .Q(out_6), .reset(Reset));  // open: Qn, preset, en
  Counter #(.width(5), .max('h1f)) counter_2 (
    .Q(counter_2_q), .clk(clock_1_out), .clr(comparator_3_gt));  // open: load, D, count, carry
  Comparator #(.width(5), .mode("unsigned")) comparator_3 (
    .a({5{1'b0}}), .b(counter_2_q), .gt(comparator_3_gt), .eq(comparator_3_eq));  // open: lt
  assign bit_extender_1_out = {{4{1'b0}}, comparator_3_eq};  // Bit_Extender bit_extender_1

  // Notes on the sheet:
  //   Odstęp
  //   Pozycja, na której ma zostać umieszczony bit "1"
endmodule
