// Logisim project generowanie_poziomu.circ as structural Verilog: 1 circuit, main circuit main
module main (
  input  Regenerate,
  output [2:0] _0,
  output [2:0] _1,
  output [2:0] _2,
  output [2:0] _3,
  output [2:0] _4,
  output [2:0] _5,
  output [2:0] _6,
  output [2:0] _7,
  output [2:0] _8,
  output [2:0] _9,
  output [2:0] _10,
  output [2:0] _11,
  output [2:0] _12,
  output [2:0] _13,
  output [2:0] _14,
  output [2:0] _15,
  output [2:0] _16,
  output [2:0] _17,
  output [2:0] _18,
  output [2:0] _19,
  output [2:0] _20,
  output [2:0] _21,
  output [2:0] _22,
  output [2:0] _23,
  output [2:0] _24,
  output [2:0] _25,
  output [2:0] _26,
  output [2:0] _27,
  output [2:0] _28,
  output [2:0] _29,
  output [2:0] _30,
  output [2:0] _31
);

  wire adder_1_cout, clock_1_out, comparator_1_gt, comparator_1_lt, comparator_2_lt, comparator_3_gt,
       controlled_buffer_3_out, demultiplexer_2_out0, demultiplexer_2_out1, demultiplexer_2_out2,
       demultiplexer_2_out3, demultiplexer_2_out4, demultiplexer_2_out5, demultiplexer_2_out6,
       demultiplexer_2_out7, demultiplexer_2_out8, demultiplexer_2_out9, demultiplexer_2_out10,
       demultiplexer_2_out11, demultiplexer_2_out12, demultiplexer_2_out13, demultiplexer_2_out14,
       demultiplexer_2_out15, demultiplexer_2_out16, demultiplexer_2_out17, demultiplexer_2_out18,
       demultiplexer_2_out19, demultiplexer_2_out20, demultiplexer_2_out21, demultiplexer_2_out22,
       demultiplexer_2_out23, demultiplexer_2_out24, demultiplexer_2_out25, demultiplexer_2_out26,
       demultiplexer_2_out27, demultiplexer_2_out28, demultiplexer_2_out29, demultiplexer_2_out30,
       demultiplexer_2_out31, not_1_out, or_1_out;
  wire [1:0] random_1_out;
  wire [2:0] adder_2_out, bit_extender_1_out, bit_extender_2_out, controlled_buffer_1_out,
       controlled_buffer_2_out, demultiplexer_1_out0, demultiplexer_1_out1, demultiplexer_1_out2,
       demultiplexer_1_out3, demultiplexer_1_out4, demultiplexer_1_out5, demultiplexer_1_out6,
       demultiplexer_1_out7, demultiplexer_1_out8, demultiplexer_1_out9, demultiplexer_1_out10,
       demultiplexer_1_out11, demultiplexer_1_out12, demultiplexer_1_out13, demultiplexer_1_out14,
       demultiplexer_1_out15, demultiplexer_1_out16, demultiplexer_1_out17, demultiplexer_1_out18,
       demultiplexer_1_out19, demultiplexer_1_out20, demultiplexer_1_out21, demultiplexer_1_out22,
       demultiplexer_1_out23, demultiplexer_1_out24, demultiplexer_1_out25, demultiplexer_1_out26,
       demultiplexer_1_out27, demultiplexer_1_out28, demultiplexer_1_out29, demultiplexer_1_out30,
       demultiplexer_1_out31, register_1_q, subtractor_1_out;
  wire [4:0] adder_1_out;
  wire [5:0] counter_1_q;

  Clock clock_1 (.out(clock_1_out));
  Random #(.width(2)) random_1 (.clk(clock_1_out), .out(random_1_out));  // open: next, clr
  Counter #(.width(6), .max('h3f), .ongoal("stay"), .trigger("falling")) counter_1 (
    .Q(counter_1_q), .clk(clock_1_out), .clr(Regenerate));  // open: load, D, count, carry
  Comparator #(.width(2), .mode("unsigned")) comparator_1 (
    .a(random_1_out), .b(2'b10), .gt(comparator_1_gt), .lt(comparator_1_lt));  // open: eq
  assign bit_extender_1_out = {{2{1'b0}}, comparator_1_lt};  // Bit_Extender bit_extender_1
  assign controlled_buffer_1_out = comparator_2_lt ? bit_extender_1_out : 3'bz;  // Controlled_Buffer controlled_buffer_1
  Pull_Resistor pull_resistor_1 (.node(controlled_buffer_1_out));
  Register #(.width(3)) register_1 (
    .D(subtractor_1_out), .Q(register_1_q), .clk(clock_1_out), .clr(Regenerate));  // open: en
  Adder #(.width(5)) adder_1 (.a(counter_1_q[4:0]), .b(5'b00100), .out(adder_1_out), .cout(adder_1_cout));  // open: cin
  assign bit_extender_2_out = {{2{1'b0}}, comparator_1_gt};  // Bit_Extender bit_extender_2
  assign controlled_buffer_2_out = comparator_3_gt ? bit_extender_2_out : 3'bz;  // Controlled_Buffer controlled_buffer_2
  Pull_Resistor pull_resistor_2 (.node(controlled_buffer_2_out));
  Adder #(.width(3)) adder_2 (.a(controlled_buffer_1_out), .b(register_1_q), .out(adder_2_out));  // open: cin, cout
  Comparator #(.width(3), .mode("unsigned")) comparator_2 (
    .a(register_1_q), .b(3'b111), .lt(comparator_2_lt));  // open: gt, eq
  Comparator #(.width(3), .mode("unsigned")) comparator_3 (
    .a(register_1_q), .b(3'b000), .gt(comparator_3_gt));  // open: eq, lt
  or or_1 (or_1_out, adder_1_cout, counter_1_q[5]);
  Subtractor #(.width(3)) subtractor_1 (
    .a(adder_2_out), .b(controlled_buffer_2_out), .out(subtractor_1_out));  // open: bin, bout
  not not_1 (not_1_out, or_1_out);
  Demultiplexer #(.select(5), .width(3)) demultiplexer_1 (
    .out0(demultiplexer_1_out0), .out1(demultiplexer_1_out1), .out2(demultiplexer_1_out2),
    .out3(demultiplexer_1_out3), .out4(demultiplexer_1_out4), .out5(demultiplexer_1_out5),
    .out6(demultiplexer_1_out6), .out7(demultiplexer_1_out7), .out8(demultiplexer_1_out8),
    .out9(demultiplexer_1_out9), .out10(demultiplexer_1_out10), .out11(demultiplexer_1_out11),
    .out12(demultiplexer_1_out12), .out13(demultiplexer_1_out13), .out14(demultiplexer_1_out14),
    .out15(demultiplexer_1_out15), .out16(demultiplexer_1_out16), .out17(demultiplexer_1_out17),
    .out18(demultiplexer_1_out18), .out19(demultiplexer_1_out19), .out20(demultiplexer_1_out20),
    .out21(demultiplexer_1_out21), .out22(demultiplexer_1_out22), .out23(demultiplexer_1_out23),
    .out24(demultiplexer_1_out24), .out25(demultiplexer_1_out25), .out26(demultiplexer_1_out26),
    .out27(demultiplexer_1_out27), .out28(demultiplexer_1_out28), .out29(demultiplexer_1_out29),
    .out30(demultiplexer_1_out30), .out31(demultiplexer_1_out31), .in(subtractor_1_out), .sel(adder_1_out));  // open: en
  assign controlled_buffer_3_out = not_1_out ? clock_1_out : 1'bz;  // Controlled_Buffer controlled_buffer_3
  Pull_Resistor pull_resistor_3 (.node(controlled_buffer_3_out));
  Register #(.width(3), .trigger("falling")) register_2 (
    .D(demultiplexer_1_out0), .Q(_0), .clk(demultiplexer_2_out0));  // open: en, clr
  Register #(.width(3)) register_3 (.D(demultiplexer_1_out1), .Q(_1), .clk(demultiplexer_2_out1));  // open: en, clr
  Register #(.width(3)) register_4 (.D(demultiplexer_1_out2), .Q(_2), .clk(demultiplexer_2_out2));  // open: en, clr
  Register #(.width(3)) register_5 (.D(demultiplexer_1_out3), .Q(_3), .clk(demultiplexer_2_out3));  // open: en, clr
  Register #(.width(3), .trigger("falling")) register_6 (
    .D(demultiplexer_1_out4), .Q(_4), .clk(demultiplexer_2_out4));  // open: en, clr
  Register #(.width(3)) register_7 (.D(demultiplexer_1_out5), .Q(_5), .clk(demultiplexer_2_out5));  // open: en, clr
  Register #(.width(3)) register_8 (.D(demultiplexer_1_out6), .Q(_6), .clk(demultiplexer_2_out6));  // open: en, clr
  Register #(.width(3)) register_9 (.D(demultiplexer_1_out7), .Q(_7), .clk(demultiplexer_2_out7));  // open: en, clr
  Register #(.width(3)) register_10 (.D(demultiplexer_1_out8), .Q(_8), .clk(demultiplexer_2_out8));  // open: en, clr
  Demultiplexer #(.select(5), .disabled(0)) demultiplexer_2 (
    .out0(demultiplexer_2_out0), .out1(demultiplexer_2_out1), .out2(demultiplexer_2_out2),
    .out3(demultiplexer_2_out3), .out4(demultiplexer_2_out4), .out5(demultiplexer_2_out5),
    .out6(demultiplexer_2_out6), .out7(demultiplexer_2_out7), .out8(demultiplexer_2_out8),
    .out9(demultiplexer_2_out9), .out10(demultiplexer_2_out10), .out11(demultiplexer_2_out11),
    .out12(demultiplexer_2_out12), .out13(demultiplexer_2_out13), .out14(demultiplexer_2_out14),
    .out15(demultiplexer_2_out15), .out16(demultiplexer_2_out16), .out17(demultiplexer_2_out17),
    .out18(demultiplexer_2_out18), .out19(demultiplexer_2_out19), .out20(demultiplexer_2_out20),
    .out21(demultiplexer_2_out21), .out22(demultiplexer_2_out22), .out23(demultiplexer_2_out23),
    .out24(demultiplexer_2_out24), .out25(demultiplexer_2_out25), .out26(demultiplexer_2_out26),
    .out27(demultiplexer_2_out27), .out28(demultiplexer_2_out28), .out29(demultiplexer_2_out29),
    .out30(demultiplexer_2_out30), .out31(demultiplexer_2_out31), .in(controlled_buffer_3_out),
    .sel(adder_1_out));  // open: en
  Register #(.width(3)) register_11 (.D(demultiplexer_1_out9), .Q(_9), .clk(demultiplexer_2_out9));  // open: en, clr
  Register #(.width(3)) register_12 (.D(demultiplexer_1_out10), .Q(_10), .clk(demultiplexer_2_out10));  // open: en, clr
  Register #(.width(3)) register_13 (.D(demultiplexer_1_out11), .Q(_11), .clk(demultiplexer_2_out11));  // open: en, clr
  Register #(.width(3)) register_14 (.D(demultiplexer_1_out12), .Q(_12), .clk(demultiplexer_2_out12));  // open: en, clr
  Register #(.width(3)) register_15 (.D(demultiplexer_1_out13), .Q(_13), .clk(demultiplexer_2_out13));  // open: en, clr
  Register #(.width(3)) register_16 (.D(demultiplexer_1_out14), .Q(_14), .clk(demultiplexer_2_out14));  // open: en, clr
  Register #(.width(3)) register_17 (.D(demultiplexer_1_out15), .Q(_15), .clk(demultiplexer_2_out15));  // open: en, clr
  Register #(.width(3)) register_18 (.D(demultiplexer_1_out16), .Q(_16), .clk(demultiplexer_2_out16));  // open: en, clr
  Register #(.width(3)) register_19 (.D(demultiplexer_1_out17), .Q(_17), .clk(demultiplexer_2_out17));  // open: en, clr
  Register #(.width(3)) register_20 (.D(demultiplexer_1_out18), .Q(_18), .clk(demultiplexer_2_out18));  // open: en, clr
  Register #(.width(3)) register_21 (.D(demultiplexer_1_out19), .Q(_19), .clk(demultiplexer_2_out19));  // open: en, clr
  Register #(.width(3)) register_22 (.D(demultiplexer_1_out20), .Q(_20), .clk(demultiplexer_2_out20));  // open: en, clr
  Register #(.width(3)) register_23 (.D(demultiplexer_1_out21), .Q(_21), .clk(demultiplexer_2_out21));  // open: en, clr
  Register #(.width(3)) register_24 (.D(demultiplexer_1_out22), .Q(_22), .clk(demultiplexer_2_out22));  // open: en, clr
  Register #(.width(3)) register_25 (.D(demultiplexer_1_out23), .Q(_23), .clk(demultiplexer_2_out23));  // open: en, clr
  Register #(.width(3)) register_26 (.D(demultiplexer_1_out24), .Q(_24), .clk(demultiplexer_2_out24));  // open: en, clr
  Register #(.width(3)) register_27 (.D(demultiplexer_1_out25), .Q(_25), .clk(demultiplexer_2_out25));  // open: en, clr
  Register #(.width(3)) register_28 (.D(demultiplexer_1_out26), .Q(_26), .clk(demultiplexer_2_out26));  // open: en, clr
  Register #(.width(3)) register_29 (.D(demultiplexer_1_out27), .Q(_27), .clk(demultiplexer_2_out27));  // open: en, clr
  Register #(.width(3)) register_30 (.D(demultiplexer_1_out28), .Q(_28), .clk(demultiplexer_2_out28));  // open: en, clr
  Register #(.width(3)) register_31 (.D(demultiplexer_1_out29), .Q(_29), .clk(demultiplexer_2_out29));  // open: en, clr
  Register #(.width(3)) register_32 (.D(demultiplexer_1_out30), .Q(_30), .clk(demultiplexer_2_out30));  // open: en, clr
  Register #(.width(3)) register_33 (.D(demultiplexer_1_out31), .Q(_31), .clk(demultiplexer_2_out31));  // open: en, clr
endmodule
