// Logisim project obsluga_zyc.circ as structural Verilog: 1 circuit, main circuit main
module main (
  input  [31:0] Enemies_input,
  input  Reset_lives,
  output [2:0] Lives,
  output is_alive,
  output [31:0] Enemies_output
);

  wire comparator_1_gt, comparator_2_eq, not_1_out, pull_resistor_1_node;
  wire [2:0] counter_1_q;

  Comparator #(.width(32), .mode("unsigned")) comparator_1 (
    .a(Enemies_input), .b(32'h7fffffff), .gt(comparator_1_gt));  // open: eq, lt
  Counter #(.width(3), .max('h7), .ongoal("stay")) counter_1 (
    .count(1'b1), .Q(counter_1_q), .clk(comparator_1_gt), .clr(pull_resistor_1_node));  // open: load, D, carry
  Pull_Resistor pull_resistor_1 (.node(pull_resistor_1_node));
  assign pull_resistor_1_node = not_1_out ? Reset_lives : 1'bz;  // Controlled_Buffer controlled_buffer_1
  not not_1 (not_1_out, is_alive);
  Subtractor #(.width(3)) subtractor_1 (.a(3'b111), .b(counter_1_q), .out(Lives));  // open: bin, bout
  Comparator #(.width(3), .mode("unsigned")) comparator_2 (
    .a(Lives), .b(3'b000), .eq(comparator_2_eq));  // open: gt, lt
  not not_2 (is_alive, comparator_2_eq);
  assign Enemies_output = is_alive ? Enemies_input : 32'bz;  // Controlled_Buffer controlled_buffer_2
  Pull_Resistor pull_resistor_2 (.node(Enemies_output));
endmodule
