// Logisim project switcher_6_bitowy.circ as structural Verilog: 1 circuit, main circuit main
module main (
  input  [5:0] Input,
  input  Button,
  output [5:0] Output
);

  wire d_ff_1_qn, d_ff_2_q, d_ff_2_qn;

  D_Flip_Flop d_ff_1 (.clk(Button), .D(d_ff_2_qn), .Qn(d_ff_1_qn));  // open: Q, preset, en, reset
  D_Flip_Flop d_ff_2 (.clk(Button), .D(d_ff_1_qn), .Q(d_ff_2_q), .Qn(d_ff_2_qn));  // open: preset, en, reset
  Demultiplexer #(.width(6)) demultiplexer_1 (.out1(Output), .in(Input), .sel(d_ff_2_q));  // open: out0, en
endmodule
