// Logisim project ustawianie_kata_wyswietlanie_kata.circ as structural Verilog: 1 circuit, main circuit main
module main (
  input  [6:0] Keyboard_input,
  input  Ground_Hit,
  output [7:0] \Liczba_jedności ,
  output [7:0] \Liczba_dziesiątek ,
  output [4:0] X,
  output [3:0] Y,
  output Activate
);

  wire and_1_out, and_2_out, clock_1_out, comparator_1_eq, comparator_2_eq, comparator_3_eq, comparator_4_eq,
       comparator_5_eq, comparator_6_eq, comparator_7_eq, comparator_8_eq, comparator_9_eq, comparator_10_eq,
       comparator_11_eq, d_ff_1_qn, d_ff_2_q, d_ff_2_qn, demultiplexer_1_out0, demultiplexer_2_out0,
       or_1_out, xor_1_out, xor_2_out;
  wire [3:0] counter_1_q, counter_2_q, register_1_q, subtractor_1_out, subtractor_2_out;
  wire [6:0] counter_3_q, multiplier_1_cout, multiplier_1_out, multiplier_2_cout, multiplier_2_out,
       multiplier_3_cout, pull_resistor_1_node, rom_2_data, rom_3_data;

  Comparator #(.width(7)) comparator_1 (.a(Keyboard_input), .b(7'b1010111), .eq(comparator_1_eq));  // open: gt, lt
  Comparator #(.width(7)) comparator_2 (.a(Keyboard_input), .b(7'b1110111), .eq(comparator_2_eq));  // open: gt, lt
  Comparator #(.width(7)) comparator_3 (.a(Keyboard_input), .b(7'b1010011), .eq(comparator_3_eq));  // open: gt, lt
  Comparator #(.width(7)) comparator_4 (.a(Keyboard_input), .b(7'b1110011), .eq(comparator_4_eq));  // open: gt, lt
  Comparator #(.width(7)) comparator_5 (.a(Keyboard_input), .b(7'b0100000), .eq(comparator_5_eq));  // open: gt, lt
  Comparator #(.width(7)) comparator_6 (.a(Keyboard_input), .b(7'b1000100), .eq(comparator_6_eq));  // open: gt, lt
  Comparator #(.width(7)) comparator_7 (.a(Keyboard_input), .b(7'b1100100), .eq(comparator_7_eq));  // open: gt, lt
  xor xor_1 (xor_1_out, comparator_1_eq, comparator_2_eq);
  xor xor_2 (xor_2_out, comparator_3_eq, comparator_4_eq);
  xor xor_3 (Activate, comparator_6_eq, comparator_7_eq);
  Demultiplexer demultiplexer_1 (.out0(demultiplexer_1_out0), .in(xor_1_out), .sel(comparator_8_eq));  // open: out1, en
  Demultiplexer demultiplexer_2 (.out0(demultiplexer_2_out0), .in(xor_2_out), .sel(comparator_9_eq));  // open: out1, en
  Counter #(.width(4), .max('hf)) counter_1 (
    .Q(counter_1_q), .clk(demultiplexer_1_out0));  // open: load, D, count, carry, clr
  Counter #(.width(4), .max('hf)) counter_2 (
    .Q(counter_2_q), .clk(demultiplexer_2_out0));  // open: load, D, count, carry, clr
  Comparator #(.width(4)) comparator_8 (.a(subtractor_1_out), .b(4'b1111), .eq(comparator_8_eq));  // open: gt, lt
  Subtractor #(.width(4)) subtractor_1 (.a(counter_1_q), .b(counter_2_q), .out(subtractor_1_out));  // open: bin, bout
  Comparator #(.width(4)) comparator_9 (.a(subtractor_1_out), .b(4'b0000), .eq(comparator_9_eq));  // open: gt, lt
  and and_1 (and_1_out, comparator_5_eq, and_2_out);
  Register #(.width(4)) register_1 (.D(subtractor_1_out), .Q(register_1_q), .clk(and_1_out));  // open: en, clr
  Clock clock_1 (.out(clock_1_out));
  ROM #(.addrWidth(4), .dataWidth(16)) rom_1 (
    .addr(subtractor_1_out), .data({\Liczba_dziesiątek , \Liczba_jedności }));  // open: sel
  Counter #(.width(7), .max('h7f)) counter_3 (
    .Q(counter_3_q), .clk(clock_1_out), .clr(and_1_out));  // open: load, D, count, carry
  or or_1 (or_1_out, and_1_out, Ground_Hit);
  D_Flip_Flop d_ff_1 (.clk(or_1_out), .D(d_ff_2_qn), .Qn(d_ff_1_qn));  // open: Q, preset, en, reset
  ROM #(.addrWidth(4), .dataWidth(7)) rom_2 (.addr(register_1_q), .data(rom_2_data));  // open: sel
  ROM #(.addrWidth(4), .dataWidth(7)) rom_3 (.addr(register_1_q), .data(rom_3_data));  // open: sel
  Pull_Resistor pull_resistor_1 (.node(pull_resistor_1_node));
  assign pull_resistor_1_node = d_ff_2_q ? counter_3_q : 7'bz;  // Controlled_Buffer controlled_buffer_1
  D_Flip_Flop d_ff_2 (.clk(or_1_out), .D(d_ff_1_qn), .Q(d_ff_2_q), .Qn(d_ff_2_qn));  // open: preset, en, reset
  Multiplier #(.width(7)) multiplier_1 (
    .a(rom_2_data), .b(pull_resistor_1_node), .out(multiplier_1_out), .cout(multiplier_1_cout));  // open: cin
  Multiplier #(.width(7)) multiplier_2 (
    .a(rom_3_data), .b(pull_resistor_1_node), .out(multiplier_2_out), .cout(multiplier_2_cout));  // open: cin
  Multiplier #(.width(7)) multiplier_3 (
    .a(pull_resistor_1_node), .b(pull_resistor_1_node), .cout(multiplier_3_cout));  // open: out, cin
  and and_2 (and_2_out, comparator_10_eq, comparator_11_eq);
  Adder #(.width(5)) adder_1 (.a(multiplier_1_cout[5:1]), .b(5'b00100), .out(X));  // open: cin, cout
  Subtractor #(.width(4)) subtractor_2 (
    .a(multiplier_2_cout[4:1]), .b(multiplier_3_cout[4:1]), .out(subtractor_2_out));  // open: bin, bout
  Adder #(.width(4)) adder_2 (.a(subtractor_2_out), .b(4'b0101), .out(Y));  // open: cin, cout
  Comparator #(.width(4), .mode("unsigned")) comparator_10 (.a(4'b0101), .b(Y), .eq(comparator_10_eq));  // open: gt, lt
  Comparator #(.width(5), .mode("unsigned")) comparator_11 (
    .a(5'b00100), .b(X), .eq(comparator_11_eq));  // open: gt, lt

  // Notes on the sheet:
  //   Ta pamięć będzie wyjściem na wyświetlacz
  //   contents of rom_1 (hex, n*v repeats v):
  //   7e67 487e 4867 3d7e 3d67 6d7e 6d67 4b7e 4b67 677e 6767 f77e f767 4c7e 4c67 7f7e
  //   X
  //   y
  //   contents of rom_2 (hex, n*v repeats v):
  //   63 61 5e 5b 57 52 4d 47 40 39 32 2a 22 1a 12 9
  //   contents of rom_3 (hex, n*v repeats v):
  //   9 12 1a 22 2a 32 39 40 47 4d 52 57 5b 5e 61 63
endmodule
